// Logisim project Computer.circ as structural Verilog: 25 circuits, main circuit main
module main (
  input  [1:0] in_1,
  input  [3:0] in_2,
  input  [3:0] in_3,
  input  [1:0] in_4,
  input  in_5
);

  wire alu_1_cout, alu_1_q0, alu_1_q1, alu_1_q2, alu_1_q3, and_1_out, and_2_out, and_3_out, and_4_out,
       and_5_out, and_6_out, and_7_out, and_8_out, and_9_out, and_10_out, and_11_out, and_12_out, and_13_out,
       and_14_out, and_15_out, and_16_out, and_17_out, and_18_out, and_19_out, and_20_out, and_21_out,
       and_22_out, and_23_out, and_24_out, and_25_out, and_26_out, button_1_out, button_2_out, button_3_out,
       control_unit_1_sr8_clock, control_unit_1_sr8_de, control_unit_1_sr8_qe, control_unit_1_sr8_reset,
       control_unit_1_sr8_w_f4, control_unit_1_tr_clock, control_unit_1_tr_res, display_driver_7_segment_1_a,
       display_driver_7_segment_1_b, display_driver_7_segment_1_c, display_driver_7_segment_1_cin,
       display_driver_7_segment_1_d, display_driver_7_segment_1_e, display_driver_7_segment_1_f,
       display_driver_7_segment_1_g, display_driver_7_segment_2_a, display_driver_7_segment_2_b,
       display_driver_7_segment_2_c, display_driver_7_segment_2_cin, display_driver_7_segment_2_d,
       display_driver_7_segment_2_e, display_driver_7_segment_2_f, display_driver_7_segment_2_g,
       double_dable_1_cen0, double_dable_1_cen1, double_dable_1_cen2, double_dable_1_cen3,
       double_dable_1_dec0, double_dable_1_dec1, double_dable_1_dec2, double_dable_1_dec3,
       double_dable_1_un0, double_dable_1_un1, double_dable_1_un2, double_dable_1_un3,
       guardar_data_1_clock_store, guardar_data_1_sr4_de, guardar_data_1_sr4_reset, not_1_out, not_2_out,
       not_3_out, not_4_out, not_5_out, not_6_out, not_7_out, not_8_out, not_9_out, not_10_out, not_11_out,
       not_12_out, not_13_out, not_14_out, not_15_out, not_16_out, not_17_out, not_18_out, or_1_out,
       or_2_out, or_3_out, or_4_out, or_5_out, or_6_out, or_7_out, or_8_out, or_9_out, or_10_out, or_11_out,
       or_12_out, or_13_out, or_14_out, or_15_out, or_16_out, or_17_out, or_18_out, or_19_out, ram_4x8_1_qed,
       registro_4_bits_1_q0, registro_4_bits_1_q1, registro_4_bits_1_q2, registro_4_bits_1_q3,
       shift_register_4_bits_1_c, shift_register_4_bits_1_q0, shift_register_4_bits_1_q1,
       shift_register_4_bits_1_q2, shift_register_4_bits_1_q3, shift_register_8_bits_1_q0,
       shift_register_8_bits_1_q1, shift_register_8_bits_1_q2, shift_register_8_bits_1_q3,
       shift_register_8_bits_1_q4, shift_register_8_bits_1_q5, shift_register_8_bits_1_q6,
       shift_register_8_bits_1_q7, temp_register_1_q0, temp_register_1_q1, temp_register_1_q2,
       temp_register_1_q3;
  wire [3:0] ram_4x8_1_bq0, ram_4x8_1_qa0;
  wire [6:0] display_driver_7_segment_3_a, display_driver_7_segment_4_a, display_driver_7_segment_5_a;

  and and_1 (and_1_out, not_1_out, in_2[0]);
  not not_1 (not_1_out, ram_4x8_1_qed);
  and and_2 (and_2_out, not_2_out, in_2[1]);
  and and_3 (and_3_out, not_3_out, in_2[2]);
  and and_4 (and_4_out, not_4_out, in_2[3]);
  not not_2 (not_2_out, ram_4x8_1_qed);
  not not_3 (not_3_out, ram_4x8_1_qed);
  not not_4 (not_4_out, ram_4x8_1_qed);
  or or_1 (or_1_out, ram_4x8_1_qa0[0], and_1_out);
  or or_2 (or_2_out, ram_4x8_1_qa0[1], and_2_out);
  or or_3 (or_3_out, ram_4x8_1_qa0[2], and_3_out);
  or or_4 (or_4_out, ram_4x8_1_qa0[3], and_4_out);
  or or_5 (or_5_out, and_18_out, temp_register_1_q0);
  or or_6 (or_6_out, and_17_out, temp_register_1_q1);
  or or_7 (or_7_out, and_16_out, temp_register_1_q2);
  display_driver_7_segment display_driver_7_segment_1 (
    .D3(or_4_out), .D2(or_3_out), .D1(or_2_out), .D0(or_1_out), .Cin(display_driver_7_segment_1_cin),
    .g(display_driver_7_segment_1_g), .f(display_driver_7_segment_1_f), .e(display_driver_7_segment_1_e),
    .d(display_driver_7_segment_1_d), .c(display_driver_7_segment_1_c), .b(display_driver_7_segment_1_b),
    .a(display_driver_7_segment_1_a));
  _7_Segment_Display u_7_segment_display_1 (
    .b(display_driver_7_segment_1_cin), .c(display_driver_7_segment_1_cin));  // open: g, f, a, e, d, dp
  or or_8 (or_8_out, and_15_out, temp_register_1_q3);
  temp_register temp_register_1 (
    .reset(control_unit_1_tr_res), .Cl(control_unit_1_tr_clock), .D7(shift_register_8_bits_1_q7),
    .D6(shift_register_8_bits_1_q6), .D5(shift_register_8_bits_1_q5), .D4(shift_register_8_bits_1_q4),
    .Q3(temp_register_1_q3), .Q2(temp_register_1_q2), .Q1(temp_register_1_q1), .Q0(temp_register_1_q0));
  Button button_1 (.out(button_1_out));
  _7_Segment_Display u_7_segment_display_2 (
    .g(display_driver_7_segment_1_g), .f(display_driver_7_segment_1_f), .a(display_driver_7_segment_1_a),
    .b(display_driver_7_segment_1_b), .e(display_driver_7_segment_1_e), .d(display_driver_7_segment_1_d),
    .c(display_driver_7_segment_1_c));  // open: dp
  not not_5 (not_5_out, in_1[0]);
  registro_4_bits registro_4_bits_1 (
    .Store(guardar_data_1_clock_store), .D3(or_4_out), .D2(or_3_out), .D1(or_2_out), .D0(or_1_out),
    .Q3(registro_4_bits_1_q3), .Q2(registro_4_bits_1_q2), .Q1(registro_4_bits_1_q1), .Q0(registro_4_bits_1_q0));
  ALU alu_1 (
    .A3(registro_4_bits_1_q3), .A2(registro_4_bits_1_q2), .A1(registro_4_bits_1_q1),
    .A0(registro_4_bits_1_q0), .Sub(in_1[0]), .B3(or_8_out), .B2(or_7_out), .B1(or_6_out), .B0(or_5_out),
    .Cout(alu_1_cout), .Q3(alu_1_q3), .Q2(alu_1_q2), .Q1(alu_1_q1), .Q0(alu_1_q0));  // open: cero
  and and_5 (and_5_out, not_5_out, alu_1_cout);
  not not_6 (not_6_out, in_1[1]);
  not not_7 (not_7_out, in_1[1]);
  and and_6 (and_6_out, alu_1_q3, not_6_out);
  and and_7 (and_7_out, and_5_out, not_7_out);
  not not_8 (not_8_out, in_1[1]);
  not not_9 (not_9_out, in_1[1]);
  and and_8 (and_8_out, alu_1_q2, not_8_out);
  and and_9 (and_9_out, alu_1_q1, not_9_out);
  guardar_data guardar_data_1 (
    .boton(button_1_out), .Clock_store(guardar_data_1_clock_store), .SR4_DE(guardar_data_1_sr4_de),
    .SR4_Reset(guardar_data_1_sr4_reset));  // open: Z
  display_driver_7_segment display_driver_7_segment_2 (
    .D3(in_3[3]), .D2(in_3[2]), .D1(in_3[1]), .D0(in_3[0]), .Cin(display_driver_7_segment_2_cin),
    .g(display_driver_7_segment_2_g), .f(display_driver_7_segment_2_f), .e(display_driver_7_segment_2_e),
    .d(display_driver_7_segment_2_d), .c(display_driver_7_segment_2_c), .b(display_driver_7_segment_2_b),
    .a(display_driver_7_segment_2_a));
  not not_10 (not_10_out, in_1[1]);
  and and_10 (and_10_out, alu_1_q0, not_10_out);
  _7_Segment_Display u_7_segment_display_3 (
    .b(display_driver_7_segment_2_cin), .c(display_driver_7_segment_2_cin));  // open: g, f, a, e, d, dp
  and and_11 (and_11_out, not_11_out, in_3[0]);
  not not_11 (not_11_out, ram_4x8_1_qed);
  _7_Segment_Display u_7_segment_display_4 (
    .g(display_driver_7_segment_2_g), .f(display_driver_7_segment_2_f), .a(display_driver_7_segment_2_a),
    .b(display_driver_7_segment_2_b), .e(display_driver_7_segment_2_e), .d(display_driver_7_segment_2_d),
    .c(display_driver_7_segment_2_c));  // open: dp
  and and_12 (and_12_out, not_12_out, in_3[1]);
  and and_13 (and_13_out, not_13_out, in_3[2]);
  and and_14 (and_14_out, not_14_out, in_3[3]);
  not not_12 (not_12_out, ram_4x8_1_qed);
  not not_13 (not_13_out, ram_4x8_1_qed);
  not not_14 (not_14_out, ram_4x8_1_qed);
  or or_9 (or_9_out, ram_4x8_1_bq0[0], and_11_out);
  or or_10 (or_10_out, ram_4x8_1_bq0[1], and_12_out);
  or or_11 (or_11_out, ram_4x8_1_bq0[2], and_13_out);
  or or_12 (or_12_out, ram_4x8_1_bq0[3], and_14_out);
  shift_register_8_bits shift_register_8_bits_1 (
    .D1(alu_1_q1), .D0(alu_1_q0), .DE(control_unit_1_sr8_de), .w_f4(control_unit_1_sr8_w_f4),
    .Clock(control_unit_1_sr8_clock), .Reset(control_unit_1_sr8_reset), .QE(control_unit_1_sr8_qe),
    .Cin(alu_1_cout), .D3(alu_1_q3), .D2(alu_1_q2), .Q6(shift_register_8_bits_1_q6),
    .Q5(shift_register_8_bits_1_q5), .Q4(shift_register_8_bits_1_q4), .Q3(shift_register_8_bits_1_q3),
    .Q2(shift_register_8_bits_1_q2), .Q1(shift_register_8_bits_1_q1), .Q0(shift_register_8_bits_1_q0),
    .Q7(shift_register_8_bits_1_q7));
  or or_13 (or_13_out, guardar_data_1_clock_store, control_unit_1_sr8_clock);
  Button button_2 (.out(button_2_out));
  shift_register_4_bits shift_register_4_bits_1 (
    .DE(guardar_data_1_sr4_de), .reset(guardar_data_1_sr4_reset), .Clock(or_13_out), .D3(or_12_out),
    .D2(or_11_out), .D1(or_10_out), .D0(or_9_out), .Q3(shift_register_4_bits_1_q3),
    .Q2(shift_register_4_bits_1_q2), .Q1(shift_register_4_bits_1_q1), .Q0(shift_register_4_bits_1_q0),
    .C(shift_register_4_bits_1_c));
  control_unit control_unit_1 (
    .Boton(button_2_out), .A(in_1[0]), .C(shift_register_4_bits_1_c), .B(in_1[1]),
    .SR8_clock(control_unit_1_sr8_clock), .SR8_DE(control_unit_1_sr8_de),
    .SR8_reset(control_unit_1_sr8_reset), .SR8_w_f4(control_unit_1_sr8_w_f4), .SR8_QE(control_unit_1_sr8_qe),
    .TR_clock(control_unit_1_tr_clock), .TR_res(control_unit_1_tr_res));
  not not_15 (not_15_out, in_1[1]);
  and and_15 (and_15_out, shift_register_4_bits_1_q3, not_15_out);
  not not_16 (not_16_out, in_1[1]);
  not not_17 (not_17_out, in_1[1]);
  and and_16 (and_16_out, shift_register_4_bits_1_q2, not_16_out);
  and and_17 (and_17_out, shift_register_4_bits_1_q1, not_17_out);
  not not_18 (not_18_out, in_1[1]);
  and and_18 (and_18_out, shift_register_4_bits_1_q0, not_18_out);
  and and_19 (and_19_out, shift_register_8_bits_1_q7, in_1[1]);
  and and_20 (and_20_out, shift_register_8_bits_1_q6, in_1[1]);
  LED led_1 (.in(and_19_out));
  LED led_2 (.in(and_20_out));
  and and_21 (and_21_out, shift_register_8_bits_1_q5, in_1[1]);
  and and_22 (and_22_out, shift_register_8_bits_1_q4, in_1[1]);
  or or_14 (or_14_out, and_22_out, and_7_out);
  LED led_3 (.in(and_21_out));
  LED led_4 (.in(or_14_out));
  and and_23 (and_23_out, shift_register_8_bits_1_q3, in_1[1]);
  and and_24 (and_24_out, shift_register_8_bits_1_q2, in_1[1]);
  or or_15 (or_15_out, and_23_out, and_6_out);
  or or_16 (or_16_out, and_24_out, and_8_out);
  LED led_5 (.in(or_15_out));
  LED led_6 (.in(or_16_out));
  _7_Segment_Display u_7_segment_display_5 (
    .g(display_driver_7_segment_5_a[6]), .f(display_driver_7_segment_5_a[5]),
    .a(display_driver_7_segment_5_a[0]), .b(display_driver_7_segment_5_a[1]),
    .e(display_driver_7_segment_5_a[4]), .d(display_driver_7_segment_5_a[3]),
    .c(display_driver_7_segment_5_a[2]));  // open: dp
  Button button_3 (.out(button_3_out));
  and and_25 (and_25_out, shift_register_8_bits_1_q1, in_1[1]);
  and and_26 (and_26_out, shift_register_8_bits_1_q0, in_1[1]);
  or or_17 (or_17_out, and_25_out, and_9_out);
  or or_18 (or_18_out, and_26_out, and_10_out);
  LED led_7 (.in(or_17_out));
  LED led_8 (.in(or_18_out));
  or or_19 (or_19_out, in_5, guardar_data_1_sr4_de);
  _7_Segment_Display u_7_segment_display_6 (
    .g(display_driver_7_segment_4_a[6]), .f(display_driver_7_segment_4_a[5]),
    .a(display_driver_7_segment_4_a[0]), .b(display_driver_7_segment_4_a[1]),
    .e(display_driver_7_segment_4_a[4]), .d(display_driver_7_segment_4_a[3]),
    .c(display_driver_7_segment_4_a[2]));  // open: dp
  _7_Segment_Display u_7_segment_display_7 (
    .g(display_driver_7_segment_3_a[6]), .f(display_driver_7_segment_3_a[5]),
    .a(display_driver_7_segment_3_a[0]), .b(display_driver_7_segment_3_a[1]),
    .e(display_driver_7_segment_3_a[4]), .d(display_driver_7_segment_3_a[3]),
    .c(display_driver_7_segment_3_a[2]));  // open: dp
  RAM_4X8 ram_4x8_1 (
    .B3(in_3[3]), .QE(in_5), .B2(in_3[2]), .B1(in_3[1]), .B0(in_3[0]), .A3(in_2[3]), .A2(in_2[2]),
    .A1(in_2[1]), .A0(in_2[0]), .Reset_clock(button_3_out), .clock_button(guardar_data_1_sr4_reset),
    .B(in_4[1]), .E(or_19_out), .A(in_4[0]), .R_W(guardar_data_1_clock_store), .QB3(ram_4x8_1_bq0[3]),
    .QB2(ram_4x8_1_bq0[2]), .QB1(ram_4x8_1_bq0[1]), .BQ0(ram_4x8_1_bq0[0]), .QA3(ram_4x8_1_qa0[3]),
    .QA2(ram_4x8_1_qa0[2]), .QA1(ram_4x8_1_qa0[1]), .QA0(ram_4x8_1_qa0[0]), .QED(ram_4x8_1_qed));  // open: Xno_uso
  double_dable double_dable_1 (
    .D0(or_18_out), .D1(or_17_out), .D2(or_16_out), .D3(or_15_out), .D4(or_14_out), .D5(and_21_out),
    .D6(and_20_out), .D7(and_19_out), .Un0(double_dable_1_un0), .Un1(double_dable_1_un1),
    .Un2(double_dable_1_un2), .Un3(double_dable_1_un3), .Dec0(double_dable_1_dec0),
    .Dec1(double_dable_1_dec1), .Dec2(double_dable_1_dec2), .Dec3(double_dable_1_dec3),
    .Cen0(double_dable_1_cen0), .Cen1(double_dable_1_cen1), .Cen2(double_dable_1_cen2),
    .Cen3(double_dable_1_cen3));
  display_driver_7_segment display_driver_7_segment_3 (
    .D3(double_dable_1_un3), .D2(double_dable_1_un2), .D1(double_dable_1_un1), .D0(double_dable_1_un0),
    .g(display_driver_7_segment_3_a[6]), .f(display_driver_7_segment_3_a[5]),
    .e(display_driver_7_segment_3_a[4]), .d(display_driver_7_segment_3_a[3]),
    .c(display_driver_7_segment_3_a[2]), .b(display_driver_7_segment_3_a[1]),
    .a(display_driver_7_segment_3_a[0]));  // open: Cin
  display_driver_7_segment display_driver_7_segment_4 (
    .D3(double_dable_1_dec3), .D2(double_dable_1_dec2), .D1(double_dable_1_dec1), .D0(double_dable_1_dec0),
    .g(display_driver_7_segment_4_a[6]), .f(display_driver_7_segment_4_a[5]),
    .e(display_driver_7_segment_4_a[4]), .d(display_driver_7_segment_4_a[3]),
    .c(display_driver_7_segment_4_a[2]), .b(display_driver_7_segment_4_a[1]),
    .a(display_driver_7_segment_4_a[0]));  // open: Cin
  display_driver_7_segment display_driver_7_segment_5 (
    .D3(double_dable_1_cen3), .D2(double_dable_1_cen2), .D1(double_dable_1_cen1), .D0(double_dable_1_cen0),
    .g(display_driver_7_segment_5_a[6]), .f(display_driver_7_segment_5_a[5]),
    .e(display_driver_7_segment_5_a[4]), .d(display_driver_7_segment_5_a[3]),
    .c(display_driver_7_segment_5_a[2]), .b(display_driver_7_segment_5_a[1]),
    .a(display_driver_7_segment_5_a[0]));  // open: Cin

  // Notes on the sheet:
  //   Boton de guardado de datos
  //   Bus de control
  //   Boton
  //   para realizar operacion
  //   00 para suma
  //   01 para restar
  //   10 para multiplicar
  //   Entrada de datos para la unidad de control
  //   RAM
  //   Seleccion de espacio de memoria 00, 01, 10, 11
  //   Habilitador de lectura
  //   Bus de datos
  //   Resetear reloj
  //   Salida
endmodule

module control_unit (
  input  A,
  input  B,
  input  Boton,
  input  C,
  output SR8_reset,
  output SR8_clock,
  output TR_clock,
  output SR8_QE,
  output TR_res,
  output SR8_DE,
  output SR8_w_f4
);

  wire and_1_out, and_2_out, and_3_out, and_4_out, and_5_out, and_6_out, and_7_out, and_8_out, and_9_out,
       and_10_out, and_11_out, and_12_out, and_13_out, and_14_out, and_15_out, and_16_out, and_17_out,
       and_18_out, and_19_out, and_20_out, and_21_out, and_23_out, and_25_out, and_26_out, and_27_out,
       and_28_out, and_29_out, clock_1_out, clock_2_out, d_ff_1_q, d_ff_2_q, d_ff_3_q, d_ff_4_q, d_ff_5_q,
       d_ff_6_q, d_ff_7_q, decoder_2x4_1_q00, decoder_2x4_1_q01, decoder_2x4_1_q10, j_k_ff_1_q, j_k_ff_1_qn,
       j_k_ff_2_q, j_k_ff_2_qn, j_k_ff_3_q, j_k_ff_3_qn, j_k_ff_4_q, j_k_ff_4_qn, j_k_ff_5_q, j_k_ff_5_qn,
       j_k_ff_6_qn, j_k_ff_7_q, j_k_ff_7_qn, j_k_ff_8_q, j_k_ff_8_qn, j_k_ff_9_q, j_k_ff_9_qn, j_k_ff_10_q,
       j_k_ff_10_qn, j_k_ff_11_qn, j_k_ff_12_q, j_k_ff_12_qn, not_1_out, not_2_out, or_1_out, or_2_out,
       or_3_out, or_4_out, or_5_out, or_6_out;

  Button button_1 ();  // open: out
  decoder_2x4 decoder_2x4_1 (
    .B(B), .A(A), .Q00(decoder_2x4_1_q00), .Q01(decoder_2x4_1_q01), .Q10(decoder_2x4_1_q10));  // open: Q11
  not not_1 (not_1_out, j_k_ff_5_q);
  Clock clock_1 (.out(clock_1_out));
  LED led_1 (.in(j_k_ff_1_q));
  LED led_2 (.in(j_k_ff_2_q));
  and and_1 (and_1_out, decoder_2x4_1_q10, and_2_out);
  and and_2 (and_2_out, not_1_out, clock_1_out);
  LED led_3 (.in(j_k_ff_3_q));
  LED led_4 (.in(j_k_ff_5_q));
  LED led_5 (.in(j_k_ff_7_q));
  or or_1 (or_1_out, j_k_ff_2_q, SR8_clock);
  or or_2 (or_2_out, decoder_2x4_1_q00, decoder_2x4_1_q01);
  D_Flip_Flop d_ff_1 (.D(j_k_ff_3_q), .clk(or_1_out), .Q(d_ff_1_q), .reset(j_k_ff_1_q));  // open: Qn, preset
  and and_3 (and_3_out, or_2_out, Boton);
  and and_4 (and_4_out, j_k_ff_7_qn, j_k_ff_5_qn, j_k_ff_3_qn, j_k_ff_2_qn);
  J_K_Flip_Flop j_k_ff_1 (
    .J(and_4_out), .K(and_4_out), .clk(and_1_out), .Q(j_k_ff_1_q), .Qn(j_k_ff_1_qn), .reset(Boton));  // open: preset
  Clock clock_2 (.out(clock_2_out));
  D_Flip_Flop d_ff_2 (.D(d_ff_1_q), .clk(or_1_out), .Q(d_ff_2_q), .reset(j_k_ff_1_q));  // open: Qn, preset
  not not_2 (not_2_out, d_ff_5_q);
  LED led_6 (.in(j_k_ff_12_q));
  LED led_7 (.in(TR_clock));
  D_Flip_Flop d_ff_3 (.D(d_ff_2_q), .clk(or_1_out), .Q(d_ff_3_q), .reset(j_k_ff_1_q));  // open: Qn, preset
  and and_5 (and_5_out, d_ff_6_q, clock_2_out);
  and and_6 (and_6_out, and_5_out, not_2_out);
  LED led_8 (.in(j_k_ff_8_q));
  LED led_9 (.in(SR8_clock));
  LED led_10 (.in(j_k_ff_10_q));
  LED led_11 (.in(j_k_ff_9_q));
  and and_7 (and_7_out, j_k_ff_5_qn, j_k_ff_2_qn, j_k_ff_1_qn, j_k_ff_3_q, j_k_ff_7_q);
  and and_8 (and_8_out, j_k_ff_7_qn, j_k_ff_5_qn, j_k_ff_1_qn, j_k_ff_3_q);
  LED led_12 (.in(j_k_ff_4_q));
  D_Flip_Flop d_ff_4 (.D(d_ff_3_q), .clk(or_1_out), .Q(d_ff_4_q), .reset(j_k_ff_1_q));  // open: Qn, preset
  J_K_Flip_Flop j_k_ff_2 (
    .J(and_7_out), .K(and_8_out), .clk(and_1_out), .Q(j_k_ff_2_q), .Qn(j_k_ff_2_qn), .reset(Boton));  // open: preset
  D_Flip_Flop d_ff_5 (.D(d_ff_4_q), .clk(or_1_out), .Q(d_ff_5_q), .reset(j_k_ff_1_q));  // open: Qn, preset
  and and_9 (and_9_out, j_k_ff_4_qn, j_k_ff_6_qn, j_k_ff_8_qn, j_k_ff_9_qn, j_k_ff_12_qn, TR_clock, j_k_ff_10_q);
  and and_10 (and_10_out, j_k_ff_7_qn, j_k_ff_5_qn, j_k_ff_2_qn, j_k_ff_1_qn);
  and and_11 (and_11_out, j_k_ff_4_qn, j_k_ff_6_qn, j_k_ff_10_qn, j_k_ff_9_q, j_k_ff_11_qn, j_k_ff_12_qn, j_k_ff_8_q);
  and and_12 (and_12_out, j_k_ff_7_qn, j_k_ff_5_qn, j_k_ff_3_qn, j_k_ff_2_qn, j_k_ff_1_q);
  or or_3 (or_3_out, and_11_out, and_9_out);
  and and_13 (and_13_out, j_k_ff_12_qn, j_k_ff_11_qn, j_k_ff_9_qn, j_k_ff_8_qn, j_k_ff_6_qn);
  or or_4 (or_4_out, j_k_ff_3_q, d_ff_7_q);
  or or_5 (or_5_out, j_k_ff_2_q, d_ff_5_q);
  J_K_Flip_Flop j_k_ff_3 (
    .J(and_12_out), .K(and_10_out), .clk(and_1_out), .Q(j_k_ff_3_q), .Qn(j_k_ff_3_qn), .reset(Boton));  // open: preset
  J_K_Flip_Flop j_k_ff_4 (
    .J(or_3_out), .K(and_13_out), .clk(and_6_out), .Q(j_k_ff_4_q), .Qn(j_k_ff_4_qn), .reset(j_k_ff_1_q));  // open: preset
  D_Flip_Flop d_ff_6 (.D(or_4_out), .clk(or_5_out), .Q(d_ff_6_q), .reset(j_k_ff_1_q));  // open: Qn, preset
  and and_14 (and_14_out, j_k_ff_7_qn, j_k_ff_3_qn, j_k_ff_2_qn, j_k_ff_1_qn);
  D_Flip_Flop d_ff_7 (.D(d_ff_6_q), .clk(or_5_out), .Q(d_ff_7_q), .reset(j_k_ff_1_q));  // open: Qn, preset
  and and_15 (and_15_out, j_k_ff_7_qn, j_k_ff_5_qn, j_k_ff_2_qn, j_k_ff_1_qn, j_k_ff_3_q);
  J_K_Flip_Flop j_k_ff_5 (
    .J(and_15_out), .K(and_14_out), .clk(and_1_out), .Q(j_k_ff_5_q), .Qn(j_k_ff_5_qn), .reset(Boton));  // open: preset
  and and_16 (and_16_out, j_k_ff_6_qn, j_k_ff_8_qn, j_k_ff_9_qn, j_k_ff_10_qn, j_k_ff_11_qn, j_k_ff_12_qn, j_k_ff_4_q);
  and and_17 (and_17_out, j_k_ff_4_qn, j_k_ff_8_qn, j_k_ff_9_qn, j_k_ff_10_qn, j_k_ff_11_qn, j_k_ff_12_qn);
  and and_18 (and_18_out, j_k_ff_5_qn, j_k_ff_2_qn, j_k_ff_1_qn, j_k_ff_3_q);
  J_K_Flip_Flop j_k_ff_6 (
    .J(and_16_out), .K(and_17_out), .clk(and_6_out), .Q(SR8_clock), .Qn(j_k_ff_6_qn), .reset(or_6_out));  // open: preset
  or or_6 (or_6_out, d_ff_7_q, j_k_ff_1_q);
  and and_19 (and_19_out, j_k_ff_7_qn, j_k_ff_5_qn, j_k_ff_3_qn, j_k_ff_2_qn, j_k_ff_1_q);
  J_K_Flip_Flop j_k_ff_7 (
    .J(and_19_out), .K(and_18_out), .clk(and_1_out), .Q(j_k_ff_7_q), .Qn(j_k_ff_7_qn), .reset(Boton));  // open: preset
  and and_20 (and_20_out, j_k_ff_6_qn, j_k_ff_8_qn, j_k_ff_9_qn, j_k_ff_11_qn, j_k_ff_12_qn, j_k_ff_10_q, j_k_ff_4_q);
  J_K_Flip_Flop j_k_ff_8 (
    .J(and_20_out), .K(and_21_out), .clk(and_6_out), .Q(j_k_ff_8_q), .Qn(j_k_ff_8_qn), .reset(j_k_ff_1_q));  // open: preset
  and and_21 (and_21_out, j_k_ff_6_qn, j_k_ff_9_qn, j_k_ff_10_qn, j_k_ff_11_qn, j_k_ff_12_qn, j_k_ff_4_q);
  and and_22 (SR8_DE, j_k_ff_8_q, C);
  or or_7 (SR8_reset, and_3_out, j_k_ff_1_q);
  and and_23 (and_23_out, j_k_ff_4_qn, j_k_ff_6_qn, j_k_ff_10_qn, j_k_ff_11_qn, j_k_ff_12_qn, j_k_ff_8_q);
  J_K_Flip_Flop j_k_ff_9 (
    .J(and_23_out), .K(and_23_out), .clk(and_6_out), .Q(j_k_ff_9_q), .Qn(j_k_ff_9_qn), .reset(j_k_ff_1_q));  // open: preset
  and and_24 (SR8_w_f4, j_k_ff_9_q, C);
  and and_25 (and_25_out, j_k_ff_4_qn, j_k_ff_6_qn, j_k_ff_8_qn, j_k_ff_9_qn, j_k_ff_10_qn, j_k_ff_11_qn, j_k_ff_12_q);
  and and_26 (and_26_out, j_k_ff_6_qn, j_k_ff_8_qn, j_k_ff_9_qn, j_k_ff_11_qn, j_k_ff_12_qn, j_k_ff_4_q);
  J_K_Flip_Flop j_k_ff_10 (
    .J(and_25_out), .K(and_26_out), .clk(and_6_out), .Q(j_k_ff_10_q), .Qn(j_k_ff_10_qn), .reset(j_k_ff_1_q));  // open: preset
  or or_8 (SR8_QE, d_ff_7_q, j_k_ff_10_q);
  and and_27 (and_27_out, j_k_ff_4_qn, j_k_ff_6_qn, j_k_ff_8_qn, j_k_ff_9_qn, j_k_ff_12_qn, j_k_ff_10_q);
  and and_28 (and_28_out, j_k_ff_4_qn, j_k_ff_6_qn, j_k_ff_8_qn, j_k_ff_9_qn, j_k_ff_12_qn, j_k_ff_10_q);
  J_K_Flip_Flop j_k_ff_11 (
    .J(and_27_out), .K(and_28_out), .clk(and_6_out), .Q(TR_clock), .Qn(j_k_ff_11_qn), .reset(j_k_ff_1_q));  // open: preset
  and and_29 (and_29_out, j_k_ff_4_qn, j_k_ff_6_qn, j_k_ff_8_qn, j_k_ff_9_qn, j_k_ff_10_qn, j_k_ff_11_qn);
  J_K_Flip_Flop j_k_ff_12 (
    .J(and_29_out), .K(and_29_out), .clk(and_6_out), .Q(j_k_ff_12_q), .Qn(j_k_ff_12_qn), .reset(j_k_ff_1_q));  // open: preset
  or or_9 (TR_res, j_k_ff_12_q, and_3_out);

  // Notes on the sheet:
  //   c
  //   b
  //   a
  //   X
  //   x
  //   Z
  //   A
  //   B
  //   Registro de control de multiplicacion
  //   C
  //   D
  //   E
  //   Anthony Lopez
  //   F
endmodule

module registro_4_bits (
  input  Store,
  input  D3,
  input  D2,
  input  D1,
  input  D0,
  output Q3,
  output Q2,
  output Q1,
  output Q0
);

  d_latch d_latch_1 (.D(D3), .S(Store), .Q(Q3));
  d_latch d_latch_2 (.D(D2), .S(Store), .Q(Q2));
  d_latch d_latch_3 (.D(D1), .S(Store), .Q(Q1));
  d_latch d_latch_4 (.D(D0), .S(Store), .Q(Q0));
endmodule

module ALU (
  input  B3,
  input  B2,
  input  B1,
  input  B0,
  input  A3,
  input  A2,
  input  A1,
  input  A0,
  input  Sub,
  output cero,
  output Cout,
  output Q3,
  output Q2,
  output Q1,
  output Q0
);

  wire not_1_out, not_2_out, not_3_out, not_4_out, xor_1_out, xor_2_out, xor_3_out, xor_4_out;

  not not_1 (not_1_out, Q3);
  not not_2 (not_2_out, Q2);
  and and_1 (cero, not_1_out, not_2_out, not_3_out, not_4_out);
  xor xor_1 (xor_1_out, Sub, B3);
  not not_3 (not_3_out, Q1);
  not not_4 (not_4_out, Q0);
  xor xor_2 (xor_2_out, Sub, B2);
  xor xor_3 (xor_3_out, Sub, B1);
  xor xor_4 (xor_4_out, Sub, B0);
  sumador_4bit sumador_4bit_1 (
    .B3(xor_1_out), .B2(xor_2_out), .B1(xor_3_out), .B0(xor_4_out), .A3(A3), .A2(A2), .A1(A1), .A0(A0),
    .Cin(Sub), .Cout(Cout), .Q3(Q3), .Q2(Q2), .Q1(Q1), .Q0(Q0));
endmodule

module binary_cell (
  input  D,
  input  S,
  input  R_W,
  output Q
);

  wire and_1_out, and_2_out, and_3_out, nor_1_out, nor_2_out, not_1_out;

  and and_1 (and_1_out, S, R_W);
  not not_1 (not_1_out, D);
  and and_2 (and_2_out, D, and_1_out);
  and and_3 (and_3_out, and_1_out, not_1_out);
  nor nor_1 (nor_1_out, and_2_out, nor_2_out);
  nor nor_2 (nor_2_out, nor_1_out, and_3_out);
  and and_4 (Q, nor_2_out, S);
endmodule

module sumador_4bit (
  input  B3,
  input  B2,
  input  B1,
  input  B0,
  input  A3,
  input  A2,
  input  A1,
  input  A0,
  input  Cin,
  output Cout,
  output Q3,
  output Q2,
  output Q1,
  output Q0
);

  wire sumador_2_cout, sumador_3_cout, sumador_4_cout;

  Sumador sumador_1 (.A(A3), .B(B3), .Cin(sumador_2_cout), .Sum(Q3), .Cout(Cout));
  Sumador sumador_2 (.A(A2), .B(B2), .Cin(sumador_3_cout), .Sum(Q2), .Cout(sumador_2_cout));
  Sumador sumador_3 (.A(A1), .B(B1), .Cin(sumador_4_cout), .Sum(Q1), .Cout(sumador_3_cout));
  Sumador sumador_4 (.A(A0), .B(B0), .Cin(Cin), .Sum(Q0), .Cout(sumador_4_cout));
endmodule

module Sumador (
  input  A,
  input  B,
  input  Cin,
  output Sum,
  output Cout
);

  wire and_1_out, and_2_out, xor_1_out;

  xor xor_1 (xor_1_out, A, B);
  and and_1 (and_1_out, B, A);
  xor xor_2 (Sum, xor_1_out, Cin);
  and and_2 (and_2_out, xor_1_out, Cin);
  or or_1 (Cout, and_2_out, and_1_out);
endmodule

module d_flip_flop (
  input  D,
  input  Clock,
  output Q
);

  wire d_latch_1_q, not_1_out;

  not not_1 (not_1_out, Clock);
  d_latch d_latch_1 (.D(D), .S(not_1_out), .Q(d_latch_1_q));
  d_latch d_latch_2 (.D(d_latch_1_q), .S(not_1_out), .Q(Q));
endmodule

module d_latch (
  input  D,
  input  S,
  output Q
);

  wire and_1_out, and_2_out, nor_1_out, not_1_out;

  and and_1 (and_1_out, D, S);
  and and_2 (and_2_out, S, not_1_out);
  not not_1 (not_1_out, D);
  nor nor_1 (nor_1_out, and_1_out, Q);
  nor nor_2 (Q, nor_1_out, and_2_out);
endmodule

module RAM_4X8 (
  input  B3,
  input  B2,
  input  B1,
  input  B0,
  input  A3,
  input  A2,
  input  A1,
  input  A0,
  input  Xno_uso,
  input  B,
  input  A,
  input  Reset_clock,
  input  clock_button,
  input  E,
  input  R_W,
  input  QE,
  output QB3,
  output QB2,
  output QB1,
  output BQ0,
  output QA3,
  output QA2,
  output QA1,
  output QA0,
  output QED
);

  wire binary_cell_1_q, binary_cell_2_q, binary_cell_3_q, binary_cell_4_q, binary_cell_5_q, binary_cell_6_q,
       binary_cell_7_q, binary_cell_8_q, binary_cell_9_q, binary_cell_10_q, binary_cell_11_q,
       binary_cell_12_q, binary_cell_13_q, binary_cell_14_q, binary_cell_15_q, binary_cell_16_q,
       binary_cell_17_q, binary_cell_18_q, binary_cell_19_q, binary_cell_20_q, binary_cell_21_q,
       binary_cell_22_q, binary_cell_23_q, binary_cell_24_q, binary_cell_25_q, binary_cell_26_q,
       binary_cell_27_q, binary_cell_28_q, binary_cell_29_q, binary_cell_30_q, binary_cell_31_q,
       binary_cell_32_q, demux_4_bits_1_q00, demux_4_bits_1_q01, demux_4_bits_1_q10, demux_4_bits_1_q11,
       j_k_ff_1_q, j_k_ff_2_q, not_1_out, or_1_out, or_2_out, or_3_out, or_4_out, or_5_out, or_6_out,
       or_7_out, or_8_out, or_9_out, or_10_out;

  J_K_Flip_Flop j_k_ff_1 (
    .J(j_k_ff_2_q), .K(j_k_ff_2_q), .clk(clock_button), .Q(j_k_ff_1_q), .reset(Reset_clock));  // open: Qn, preset
  not not_1 (not_1_out, Xno_uso);
  J_K_Flip_Flop j_k_ff_2 (
    .J(not_1_out), .K(not_1_out), .clk(clock_button), .Q(j_k_ff_2_q), .reset(Reset_clock));  // open: Qn, preset
  or or_1 (or_1_out, j_k_ff_2_q, A);
  or or_2 (or_2_out, B, j_k_ff_1_q);
  demux_4_bits demux_4_bits_1 (
    .A(or_1_out), .B(or_2_out), .E(E), .Q00(demux_4_bits_1_q00), .Q01(demux_4_bits_1_q01),
    .Q10(demux_4_bits_1_q10), .Q11(demux_4_bits_1_q11));
  binary_cell binary_cell_1 (.D(B3), .S(demux_4_bits_1_q00), .R_W(R_W), .Q(binary_cell_1_q));
  binary_cell binary_cell_2 (.D(B3), .S(demux_4_bits_1_q01), .R_W(R_W), .Q(binary_cell_2_q));
  binary_cell binary_cell_3 (.D(B3), .S(demux_4_bits_1_q10), .R_W(R_W), .Q(binary_cell_3_q));
  binary_cell binary_cell_4 (.D(B3), .S(demux_4_bits_1_q11), .R_W(R_W), .Q(binary_cell_4_q));
  or or_3 (or_3_out, binary_cell_4_q, binary_cell_3_q, binary_cell_2_q, binary_cell_1_q);
  binary_cell binary_cell_5 (.D(B2), .S(demux_4_bits_1_q00), .R_W(R_W), .Q(binary_cell_5_q));
  binary_cell binary_cell_6 (.D(B2), .S(demux_4_bits_1_q01), .R_W(R_W), .Q(binary_cell_6_q));
  binary_cell binary_cell_7 (.D(B2), .S(demux_4_bits_1_q10), .R_W(R_W), .Q(binary_cell_7_q));
  binary_cell binary_cell_8 (.D(B2), .S(demux_4_bits_1_q11), .R_W(R_W), .Q(binary_cell_8_q));
  or or_4 (or_4_out, binary_cell_8_q, binary_cell_7_q, binary_cell_6_q, binary_cell_5_q);
  and and_1 (QB3, QE, or_3_out);
  and and_2 (QB2, QE, or_4_out);
  and and_3 (QB1, QE, or_5_out);
  binary_cell binary_cell_9 (.D(B1), .S(demux_4_bits_1_q00), .R_W(R_W), .Q(binary_cell_9_q));
  binary_cell binary_cell_10 (.D(B1), .S(demux_4_bits_1_q01), .R_W(R_W), .Q(binary_cell_10_q));
  binary_cell binary_cell_11 (.D(B1), .S(demux_4_bits_1_q10), .R_W(R_W), .Q(binary_cell_11_q));
  binary_cell binary_cell_12 (.D(B1), .S(demux_4_bits_1_q11), .R_W(R_W), .Q(binary_cell_12_q));
  or or_5 (or_5_out, binary_cell_12_q, binary_cell_11_q, binary_cell_10_q, binary_cell_9_q);
  and and_4 (BQ0, QE, or_6_out);
  binary_cell binary_cell_13 (.D(B0), .S(demux_4_bits_1_q00), .R_W(R_W), .Q(binary_cell_13_q));
  binary_cell binary_cell_14 (.D(B0), .S(demux_4_bits_1_q01), .R_W(R_W), .Q(binary_cell_14_q));
  binary_cell binary_cell_15 (.D(B0), .S(demux_4_bits_1_q10), .R_W(R_W), .Q(binary_cell_15_q));
  binary_cell binary_cell_16 (.D(B0), .S(demux_4_bits_1_q11), .R_W(R_W), .Q(binary_cell_16_q));
  or or_6 (or_6_out, binary_cell_16_q, binary_cell_15_q, binary_cell_14_q, binary_cell_13_q);
  binary_cell binary_cell_17 (.D(A3), .S(demux_4_bits_1_q00), .R_W(R_W), .Q(binary_cell_17_q));
  binary_cell binary_cell_18 (.D(A3), .S(demux_4_bits_1_q01), .R_W(R_W), .Q(binary_cell_18_q));
  binary_cell binary_cell_19 (.D(A3), .S(demux_4_bits_1_q10), .R_W(R_W), .Q(binary_cell_19_q));
  binary_cell binary_cell_20 (.D(A3), .S(demux_4_bits_1_q11), .R_W(R_W), .Q(binary_cell_20_q));
  or or_7 (or_7_out, binary_cell_20_q, binary_cell_19_q, binary_cell_18_q, binary_cell_17_q);
  binary_cell binary_cell_21 (.D(A2), .S(demux_4_bits_1_q00), .R_W(R_W), .Q(binary_cell_21_q));
  binary_cell binary_cell_22 (.D(A2), .S(demux_4_bits_1_q01), .R_W(R_W), .Q(binary_cell_22_q));
  binary_cell binary_cell_23 (.D(A2), .S(demux_4_bits_1_q10), .R_W(R_W), .Q(binary_cell_23_q));
  binary_cell binary_cell_24 (.D(A2), .S(demux_4_bits_1_q11), .R_W(R_W), .Q(binary_cell_24_q));
  or or_8 (or_8_out, binary_cell_24_q, binary_cell_23_q, binary_cell_22_q, binary_cell_21_q);
  and and_5 (QA3, QE, or_7_out);
  and and_6 (QA2, QE, or_8_out);
  and and_7 (QA1, QE, or_9_out);
  binary_cell binary_cell_25 (.D(A1), .S(demux_4_bits_1_q00), .R_W(R_W), .Q(binary_cell_25_q));
  binary_cell binary_cell_26 (.D(A1), .S(demux_4_bits_1_q01), .R_W(R_W), .Q(binary_cell_26_q));
  binary_cell binary_cell_27 (.D(A1), .S(demux_4_bits_1_q10), .R_W(R_W), .Q(binary_cell_27_q));
  binary_cell binary_cell_28 (.D(A1), .S(demux_4_bits_1_q11), .R_W(R_W), .Q(binary_cell_28_q));
  or or_9 (or_9_out, binary_cell_28_q, binary_cell_27_q, binary_cell_26_q, binary_cell_25_q);
  and and_8 (QA0, QE, or_10_out);
  binary_cell binary_cell_29 (.D(A0), .S(demux_4_bits_1_q00), .R_W(R_W), .Q(binary_cell_29_q));
  binary_cell binary_cell_30 (.D(A0), .S(demux_4_bits_1_q01), .R_W(R_W), .Q(binary_cell_30_q));
  binary_cell binary_cell_31 (.D(A0), .S(demux_4_bits_1_q10), .R_W(R_W), .Q(binary_cell_31_q));
  binary_cell binary_cell_32 (.D(A0), .S(demux_4_bits_1_q11), .R_W(R_W), .Q(binary_cell_32_q));
  or or_10 (or_10_out, binary_cell_32_q, binary_cell_31_q, binary_cell_30_q, binary_cell_29_q);

  assign QED = QE;
endmodule

module decoder_2x4 (
  input  B,
  input  A,
  output Q00,
  output Q01,
  output Q10,
  output Q11
);

  wire not_1_out, not_2_out;

  not not_1 (not_1_out, B);
  not not_2 (not_2_out, A);
  and and_1 (Q00, not_1_out, not_2_out);
  and and_2 (Q01, not_1_out, A);
  and and_3 (Q10, B, not_2_out);
  and and_4 (Q11, B, A);
endmodule

module flag (
  input  in_1,
  input  in_2,
  output out_3,
  output out_4,
  output out_5,
  output out_6,
  output out_7
);

  wire button_1_out, not_1_out, registro_4_bits_1_q0, registro_4_bits_1_q1, registro_4_bits_1_q2,
       registro_4_bits_1_q3, registro_4_bits_2_q0, registro_4_bits_2_q1, registro_4_bits_2_q2,
       registro_4_bits_2_q3, sumador_4bit_1_cout;

  sumador_4bit sumador_4bit_1 (
    .B3(registro_4_bits_1_q3), .B2(registro_4_bits_1_q2), .B1(registro_4_bits_1_q1),
    .B0(registro_4_bits_1_q0), .A0(in_1), .Cout(sumador_4bit_1_cout));  // open: A3, A2, A1, Cin, Q3, Q2, Q1, Q0
  registro_4_bits registro_4_bits_1 (
    .Store(not_1_out), .D3(out_6), .D2(out_5), .D1(out_4), .D0(out_3), .Q3(registro_4_bits_1_q3),
    .Q2(registro_4_bits_1_q2), .Q1(registro_4_bits_1_q1), .Q0(registro_4_bits_1_q0));
  Button button_1 (.out(button_1_out));
  D_Flip_Flop d_ff_1 (.D(in_2), .clk(button_1_out));  // open: Q, Qn, preset, reset
  not not_1 (not_1_out, in_1);
  D_Flip_Flop d_ff_2 (.clk(button_1_out));  // open: D, Q, Qn, preset, reset
  D_Flip_Flop d_ff_3 (.clk(button_1_out));  // open: D, Q, Qn, preset, reset
  D_Flip_Flop d_ff_4 (.clk(button_1_out));  // open: D, Q, Qn, preset, reset
  registro_4_bits registro_4_bits_2 (
    .Store(in_1), .Q3(registro_4_bits_2_q3), .Q2(registro_4_bits_2_q2), .Q1(registro_4_bits_2_q1),
    .Q0(registro_4_bits_2_q0));  // open: D3, D2, D1, D0
  registro_4_bits registro_4_bits_3 (
    .Store(sumador_4bit_1_cout), .D0(sumador_4bit_1_cout), .Q0(out_7));  // open: D3, D2, D1, Q3, Q2, Q1

  // Notes on the sheet:
  //   Flag contara cuantas operaciones intentamos realizar
endmodule

module master_s_jk_flip_flop (
  input  J,
  input  in_2,
  input  K,
  output Q,
  output Qn
);

  wire and_1_out, and_2_out, and_3_out, and_4_out, nor_2_out, nor_4_out, not_1_out;

  and and_1 (and_1_out, nor_4_out, J, in_2);
  and and_2 (and_2_out, in_2, K, Qn);
  not not_1 (not_1_out, in_2);
  nor nor_1 (Q, and_1_out, nor_2_out);
  nor nor_2 (nor_2_out, Q, and_2_out);
  and and_3 (and_3_out, Q, not_1_out);
  and and_4 (and_4_out, not_1_out, nor_2_out);
  nor nor_3 (Qn, and_3_out, nor_4_out);
  nor nor_4 (nor_4_out, Qn, and_4_out);
endmodule

module demux_4_bits (
  input  A,
  input  B,
  input  E,
  output Q00,
  output Q01,
  output Q10,
  output Q11
);

  wire not_1_out, not_2_out;

  not not_1 (not_1_out, A);
  not not_2 (not_2_out, B);
  and and_1 (Q00, E, not_2_out, not_1_out);
  and and_2 (Q01, E, not_2_out, A);
  and and_3 (Q10, E, B, not_1_out);
  and and_4 (Q11, E, B, A);
endmodule

module display_driver_7_segment (
  input  D3,
  input  D2,
  input  D1,
  input  D0,
  output Cin,
  output g,
  output f,
  output e,
  output d,
  output c,
  output b,
  output a
);

  wire and_1_out, and_2_out, and_3_out, and_4_out, and_5_out, and_6_out, and_7_out, and_8_out, and_9_out,
       and_10_out, and_11_out, and_12_out, and_13_out, and_14_out, and_15_out, and_16_out, and_17_out,
       and_18_out, and_19_out, and_20_out, and_21_out, and_22_out, and_23_out, and_24_out, and_25_out,
       and_26_out, and_27_out, and_28_out, and_29_out, and_30_out, and_31_out, not_1_out, not_2_out,
       not_3_out, not_4_out, or_2_out, or_4_out, or_5_out, or_6_out, or_7_out, or_8_out, or_11_out,
       or_12_out, or_13_out, or_17_out;

  and and_1 (and_1_out, D3, not_3_out, D2);
  and and_2 (and_2_out, D3, D1);
  or or_1 (Cin, and_1_out, and_2_out);
  or or_2 (or_2_out, not_2_out, D0);
  and and_3 (and_3_out, not_1_out, D1, or_2_out);
  or or_3 (g, and_3_out, and_5_out, or_5_out);
  or or_4 (or_4_out, not_3_out, D3);
  and and_4 (and_4_out, not_1_out, D2, D1, not_4_out);
  and and_5 (and_5_out, D2, or_4_out);
  and and_6 (and_6_out, D3, not_2_out, not_3_out);
  or or_5 (or_5_out, and_4_out, and_6_out);
  and and_7 (and_7_out, not_2_out, not_3_out);
  or or_6 (or_6_out, and_7_out, and_9_out);
  and and_8 (and_8_out, D3, or_6_out);
  or or_7 (or_7_out, and_8_out, and_10_out, and_11_out);
  and and_9 (and_9_out, not_2_out, not_4_out);
  or or_8 (or_8_out, D2, not_4_out);
  and and_10 (and_10_out, or_8_out, not_1_out, not_3_out);
  or or_9 (f, or_7_out, and_13_out);
  and and_11 (and_11_out, not_1_out, D2, not_4_out);
  and and_12 (and_12_out, not_2_out, not_4_out);
  and and_13 (and_13_out, D3, D2, D1);
  and and_14 (and_14_out, D3, not_3_out, not_4_out);
  and and_15 (and_15_out, not_1_out, D1, not_4_out);
  or or_10 (e, and_12_out, and_15_out, and_14_out);
  and and_16 (and_16_out, not_1_out, D1);
  or or_11 (or_11_out, and_16_out, not_4_out);
  and and_17 (and_17_out, or_11_out, not_2_out);
  and and_18 (and_18_out, D2, D0);
  or or_12 (or_12_out, and_18_out, not_3_out);
  and and_19 (and_19_out, or_12_out, D3);
  or or_13 (or_13_out, and_17_out, and_19_out, and_20_out);
  or or_14 (d, or_13_out, and_21_out);
  and and_20 (and_20_out, D2, not_3_out, D0);
  and and_21 (and_21_out, not_1_out, D1, not_4_out);
  and and_22 (and_22_out, not_1_out, not_3_out);
  or or_15 (c, D0, and_22_out, and_23_out, and_24_out);
  and and_23 (and_23_out, D2, D1);
  and and_24 (and_24_out, D3, not_2_out);
  or or_16 (b, not_2_out, and_25_out, and_26_out, and_27_out);
  and and_25 (and_25_out, not_3_out, not_4_out);
  and and_26 (and_26_out, not_1_out, D1, D0);
  or or_17 (or_17_out, not_3_out, not_4_out);
  and and_27 (and_27_out, D3, or_17_out);
  and and_28 (and_28_out, not_2_out, not_4_out);
  and and_29 (and_29_out, not_1_out, D1);
  or or_18 (a, and_28_out, and_29_out, and_30_out, and_31_out);
  and and_30 (and_30_out, D2, D0);
  and and_31 (and_31_out, D3, not_3_out);
  not not_1 (not_1_out, D3);
  not not_2 (not_2_out, D2);
  not not_3 (not_3_out, D1);
  not not_4 (not_4_out, D0);
endmodule

module dlatch_2 (
  input  S,
  input  D,
  input  Clock,
  input  R,
  output Q,
  output Qn
);

  wire nand_1_out, nand_2_out, not_1_out, or_1_out, or_2_out;

  not not_1 (not_1_out, D);
  or or_1 (or_1_out, S, D);
  or or_2 (or_2_out, not_1_out, R);
  nand nand_1 (nand_1_out, or_1_out, Clock);
  nand nand_2 (nand_2_out, Clock, or_2_out);
  nand nand_3 (Q, nand_1_out, Qn);
  nand nand_4 (Qn, Q, nand_2_out);
endmodule

module Multiplier_cu_register (
  input  Reset,
  input  E_counter,
  input  counter_clock,
  output SR8_clock,
  output TR_clock,
  output TR_res,
  output SR8_DE,
  output SR8_w_f4,
  output SR8_QE,
  output M_end
);

  wire and_1_out, and_2_out, and_3_out, and_4_out, and_5_out, and_6_out, and_7_out, and_8_out, and_9_out,
       and_10_out, and_11_out, and_12_out, and_13_out, and_14_out, and_15_out, clock_1_out, d_ff_1_q,
       d_ff_2_q, d_ff_3_q, d_ff_4_q, d_ff_5_q, d_ff_6_q, j_k_ff_1_q, j_k_ff_1_qn, j_k_ff_2_qn, j_k_ff_3_qn,
       j_k_ff_4_qn, j_k_ff_5_q, j_k_ff_5_qn, j_k_ff_6_qn, j_k_ff_7_qn, not_1_out, or_1_out, or_2_out,
       or_3_out, or_4_out, or_5_out;

  or or_1 (or_1_out, counter_clock, SR8_clock);
  D_Flip_Flop d_ff_1 (.D(E_counter), .clk(or_1_out), .Q(d_ff_1_q), .reset(Reset));  // open: Qn, preset
  Clock clock_1 (.out(clock_1_out));
  D_Flip_Flop d_ff_2 (.D(d_ff_1_q), .clk(or_1_out), .Q(d_ff_2_q), .reset(Reset));  // open: Qn, preset
  not not_1 (not_1_out, d_ff_5_q);
  LED led_1 (.in(TR_res));
  LED led_2 (.in(TR_clock));
  D_Flip_Flop d_ff_3 (.D(d_ff_2_q), .clk(or_1_out), .Q(d_ff_3_q), .reset(Reset));  // open: Qn, preset
  and and_1 (and_1_out, d_ff_6_q, clock_1_out);
  and and_2 (and_2_out, and_1_out, not_1_out);
  LED led_3 (.in(j_k_ff_5_q));
  LED led_4 (.in(SR8_w_f4));
  LED led_5 (.in(SR8_DE));
  LED led_6 (.in(SR8_clock));
  LED led_7 (.in(j_k_ff_1_q));
  D_Flip_Flop d_ff_4 (.D(d_ff_3_q), .clk(or_1_out), .Q(d_ff_4_q), .reset(Reset));  // open: Qn, preset
  D_Flip_Flop d_ff_5 (.D(d_ff_4_q), .clk(or_1_out), .Q(d_ff_5_q), .reset(Reset));  // open: Qn, preset
  and and_3 (and_3_out, j_k_ff_1_qn, j_k_ff_2_qn, j_k_ff_3_qn, j_k_ff_4_qn, j_k_ff_7_qn, TR_clock, j_k_ff_5_q);
  and and_4 (and_4_out, j_k_ff_1_qn, j_k_ff_2_qn, j_k_ff_5_qn, SR8_w_f4, j_k_ff_6_qn, j_k_ff_7_qn, SR8_DE);
  or or_2 (or_2_out, and_4_out, and_3_out);
  or or_3 (or_3_out, E_counter, M_end);
  or or_4 (or_4_out, counter_clock, d_ff_5_q);
  and and_5 (and_5_out, j_k_ff_7_qn, j_k_ff_6_qn, j_k_ff_4_qn, j_k_ff_3_qn, j_k_ff_2_qn);
  D_Flip_Flop d_ff_6 (.D(or_3_out), .clk(or_4_out), .Q(d_ff_6_q), .reset(Reset));  // open: Qn, preset
  J_K_Flip_Flop j_k_ff_1 (
    .J(or_2_out), .K(and_5_out), .clk(and_2_out), .Q(j_k_ff_1_q), .Qn(j_k_ff_1_qn), .reset(Reset));  // open: preset
  D_Flip_Flop d_ff_7 (.D(d_ff_6_q), .clk(or_4_out), .Q(M_end), .reset(Reset));  // open: Qn, preset
  and and_6 (and_6_out, j_k_ff_2_qn, j_k_ff_3_qn, j_k_ff_4_qn, j_k_ff_5_qn, j_k_ff_6_qn, j_k_ff_7_qn, j_k_ff_1_q);
  J_K_Flip_Flop j_k_ff_2 (
    .J(and_6_out), .K(and_7_out), .clk(and_2_out), .Q(SR8_clock), .Qn(j_k_ff_2_qn), .reset(or_5_out));  // open: preset
  and and_7 (and_7_out, j_k_ff_1_qn, j_k_ff_3_qn, j_k_ff_4_qn, j_k_ff_5_qn, j_k_ff_6_qn, j_k_ff_7_qn);
  or or_5 (or_5_out, M_end, Reset);
  and and_8 (and_8_out, j_k_ff_2_qn, j_k_ff_3_qn, j_k_ff_4_qn, j_k_ff_6_qn, j_k_ff_7_qn, j_k_ff_5_q, j_k_ff_1_q);
  and and_9 (and_9_out, j_k_ff_2_qn, j_k_ff_4_qn, j_k_ff_5_qn, j_k_ff_6_qn, j_k_ff_7_qn, j_k_ff_1_q);
  J_K_Flip_Flop j_k_ff_3 (
    .J(and_8_out), .K(and_9_out), .clk(and_2_out), .Q(SR8_DE), .Qn(j_k_ff_3_qn), .reset(Reset));  // open: preset
  and and_10 (and_10_out, j_k_ff_1_qn, j_k_ff_2_qn, j_k_ff_5_qn, j_k_ff_6_qn, j_k_ff_7_qn, SR8_DE);
  J_K_Flip_Flop j_k_ff_4 (
    .J(and_10_out), .K(and_10_out), .clk(and_2_out), .Q(SR8_w_f4), .Qn(j_k_ff_4_qn), .reset(Reset));  // open: preset
  and and_11 (and_11_out, j_k_ff_1_qn, j_k_ff_2_qn, j_k_ff_3_qn, j_k_ff_4_qn, j_k_ff_5_qn, j_k_ff_6_qn, TR_res);
  and and_12 (and_12_out, j_k_ff_2_qn, j_k_ff_3_qn, j_k_ff_4_qn, j_k_ff_6_qn, j_k_ff_7_qn, j_k_ff_1_q);
  J_K_Flip_Flop j_k_ff_5 (
    .J(and_11_out), .K(and_12_out), .clk(and_2_out), .Q(j_k_ff_5_q), .Qn(j_k_ff_5_qn), .reset(Reset));  // open: preset
  or or_6 (SR8_QE, M_end, j_k_ff_5_q);
  and and_13 (and_13_out, j_k_ff_1_qn, j_k_ff_2_qn, j_k_ff_3_qn, j_k_ff_4_qn, j_k_ff_7_qn, j_k_ff_5_q);
  and and_14 (and_14_out, j_k_ff_1_qn, j_k_ff_2_qn, j_k_ff_3_qn, j_k_ff_4_qn, j_k_ff_7_qn, j_k_ff_5_q);
  J_K_Flip_Flop j_k_ff_6 (
    .J(and_13_out), .K(and_14_out), .clk(and_2_out), .Q(TR_clock), .Qn(j_k_ff_6_qn), .reset(Reset));  // open: preset
  and and_15 (and_15_out, j_k_ff_1_qn, j_k_ff_2_qn, j_k_ff_3_qn, j_k_ff_4_qn, j_k_ff_5_qn, j_k_ff_6_qn);
  J_K_Flip_Flop j_k_ff_7 (
    .J(and_15_out), .K(and_15_out), .clk(and_2_out), .Q(TR_res), .Qn(j_k_ff_7_qn), .reset(Reset));  // open: preset

  // Notes on the sheet:
  //   X
  //   A
  //   B
  //   C
  //   D
  //   E
  //   Anthony Lopez 3-743-1884
  //   F
endmodule

module shift_register_8_bits (
  input  Cin,
  input  D3,
  input  D2,
  input  D1,
  input  D0,
  input  DE,
  input  w_f4,
  input  Clock,
  input  Reset,
  input  QE,
  output Q7,
  output Q6,
  output Q5,
  output Q4,
  output Q3,
  output Q2,
  output Q1,
  output Q0
);

  wire and_1_out, and_2_out, and_3_out, and_4_out, and_5_out, and_7_out, and_8_out, and_10_out, and_11_out,
       d_ff_1_q, d_ff_2_q, d_ff_3_q, d_ff_4_q, d_ff_5_q, d_ff_6_q, d_ff_7_q, d_ff_8_q, d_ff_9_q, not_1_out,
       not_2_out, not_3_out, not_4_out, or_1_out, or_2_out, or_3_out, or_4_out, or_5_out, or_6_out, or_7_out,
       or_8_out, or_9_out;

  and and_1 (and_1_out, DE, Cin);
  D_Flip_Flop d_ff_1 (.D(and_1_out), .clk(or_1_out), .Q(d_ff_1_q), .reset(Reset));  // open: Qn, preset
  or or_1 (or_1_out, w_f4, Clock);
  not not_1 (not_1_out, DE);
  and and_2 (and_2_out, DE, D3);
  or or_2 (or_2_out, and_2_out, and_3_out);
  and and_3 (and_3_out, not_1_out, d_ff_1_q);
  D_Flip_Flop d_ff_2 (.D(or_2_out), .clk(or_3_out), .Q(d_ff_2_q), .reset(Reset));  // open: Qn, preset
  or or_3 (or_3_out, w_f4, Clock);
  not not_2 (not_2_out, DE);
  and and_4 (and_4_out, DE, D2);
  or or_4 (or_4_out, and_4_out, and_5_out);
  and and_5 (and_5_out, not_2_out, d_ff_2_q);
  or or_5 (or_5_out, w_f4, Clock);
  and and_6 (Q7, QE, or_4_out);
  D_Flip_Flop d_ff_3 (.D(or_4_out), .clk(or_5_out), .Q(d_ff_3_q), .reset(Reset));  // open: Qn, preset
  and and_7 (and_7_out, DE, D1);
  not not_3 (not_3_out, DE);
  and and_8 (and_8_out, not_3_out, d_ff_3_q);
  or or_6 (or_6_out, and_7_out, and_8_out);
  D_Flip_Flop d_ff_4 (.D(or_6_out), .clk(or_7_out), .Q(d_ff_4_q), .reset(Reset));  // open: Qn, preset
  or or_7 (or_7_out, w_f4, Clock);
  and and_9 (Q6, QE, or_6_out);
  not not_4 (not_4_out, DE);
  and and_10 (and_10_out, DE, D0);
  and and_11 (and_11_out, not_4_out, d_ff_4_q);
  and and_12 (Q5, QE, or_8_out);
  or or_8 (or_8_out, and_10_out, and_11_out);
  D_Flip_Flop d_ff_5 (.D(or_8_out), .clk(or_9_out), .Q(d_ff_5_q), .reset(Reset));  // open: Qn, preset
  or or_9 (or_9_out, w_f4, Clock);
  and and_13 (Q4, QE, d_ff_5_q);
  D_Flip_Flop d_ff_6 (.D(d_ff_5_q), .clk(Clock), .Q(d_ff_6_q), .reset(Reset));  // open: Qn, preset
  and and_14 (Q3, QE, d_ff_6_q);
  D_Flip_Flop d_ff_7 (.D(d_ff_6_q), .clk(Clock), .Q(d_ff_7_q), .reset(Reset));  // open: Qn, preset
  and and_15 (Q2, QE, d_ff_7_q);
  D_Flip_Flop d_ff_8 (.D(d_ff_7_q), .clk(Clock), .Q(d_ff_8_q), .reset(Reset));  // open: Qn, preset
  and and_16 (Q1, QE, d_ff_8_q);
  D_Flip_Flop d_ff_9 (.D(d_ff_8_q), .clk(Clock), .Q(d_ff_9_q), .reset(Reset));  // open: Qn, preset
  and and_17 (Q0, QE, d_ff_9_q);
endmodule

module shift_register_4_bits (
  input  D3,
  input  D2,
  input  D1,
  input  D0,
  input  DE,
  input  reset,
  input  Clock,
  output C,
  output Q3,
  output Q2,
  output Q1,
  output Q0
);

  wire and_1_out, and_2_out, and_3_out, and_4_out, or_1_out, or_2_out, or_3_out;

  and and_1 (and_1_out, DE, D3);
  D_Flip_Flop d_ff_1 (.D(and_1_out), .clk(Clock), .Q(Q3), .reset(reset));  // open: Qn, preset
  and and_2 (and_2_out, DE, D2);
  or or_1 (or_1_out, and_2_out, Q3);
  D_Flip_Flop d_ff_2 (.D(or_1_out), .clk(Clock), .Q(Q2), .reset(reset));  // open: Qn, preset
  and and_3 (and_3_out, DE, D1);
  or or_2 (or_2_out, and_3_out, Q2);
  D_Flip_Flop d_ff_3 (.D(or_2_out), .clk(Clock), .Q(Q1), .reset(reset));  // open: Qn, preset
  and and_4 (and_4_out, DE, D0);
  or or_3 (or_3_out, and_4_out, Q1);
  D_Flip_Flop d_ff_4 (.D(or_3_out), .clk(Clock), .Q(C), .reset(reset));  // open: Qn, preset

  assign Q0 = C;
endmodule

module temp_register (
  input  D7,
  input  D6,
  input  D5,
  input  D4,
  input  reset,
  input  Cl,
  output Q3,
  output Q2,
  output Q1,
  output Q0
);

  wire d_ff_1_q, d_ff_2_q, d_ff_3_q;

  D_Flip_Flop d_ff_1 (.D(D7), .clk(Cl), .Q(d_ff_1_q), .reset(reset));  // open: Qn, preset
  or or_1 (Q3, D6, d_ff_1_q);
  D_Flip_Flop d_ff_2 (.D(Q3), .clk(Cl), .Q(d_ff_2_q), .reset(reset));  // open: Qn, preset
  or or_2 (Q2, D5, d_ff_2_q);
  D_Flip_Flop d_ff_3 (.D(Q2), .clk(Cl), .Q(d_ff_3_q), .reset(reset));  // open: Qn, preset
  or or_3 (Q1, D4, d_ff_3_q);
  D_Flip_Flop d_ff_4 (.D(Q1), .clk(Cl), .Q(Q0), .reset(reset));  // open: Qn, preset
endmodule

module Start_up (
  input  in_1
);

  wire and_1_out, and_2_out, and_3_out, and_4_out, and_5_out, and_6_out, and_7_out, and_8_out, and_9_out,
       and_10_out, and_11_out, button_1_out, clock_1_out, j_k_ff_1_q, j_k_ff_1_qn, j_k_ff_2_q, j_k_ff_2_qn,
       j_k_ff_3_q, j_k_ff_3_qn, j_k_ff_4_q, j_k_ff_4_qn, j_k_ff_5_q, j_k_ff_5_qn, not_1_out;

  Button button_1 (.out(button_1_out));
  not not_1 (not_1_out, j_k_ff_4_q);
  Clock clock_1 (.out(clock_1_out));
  LED led_1 (.in(j_k_ff_1_q));
  LED led_2 (.in(j_k_ff_2_q));
  and and_1 (and_1_out, in_1, and_2_out);
  and and_2 (and_2_out, not_1_out, clock_1_out);
  LED led_3 (.in(j_k_ff_3_q));
  LED led_4 (.in(j_k_ff_4_q));
  LED led_5 (.in(j_k_ff_5_q));
  and and_3 (and_3_out, j_k_ff_5_qn, j_k_ff_4_qn, j_k_ff_3_qn, j_k_ff_2_qn);
  J_K_Flip_Flop j_k_ff_1 (
    .J(and_3_out), .K(and_3_out), .clk(and_1_out), .Q(j_k_ff_1_q), .Qn(j_k_ff_1_qn), .reset(button_1_out));  // open: preset
  and and_4 (and_4_out, j_k_ff_4_qn, j_k_ff_2_qn, j_k_ff_1_qn, j_k_ff_3_q, j_k_ff_5_q);
  and and_5 (and_5_out, j_k_ff_5_qn, j_k_ff_4_qn, j_k_ff_1_qn, j_k_ff_3_q);
  J_K_Flip_Flop j_k_ff_2 (
    .J(and_4_out), .K(and_5_out), .clk(and_1_out), .Q(j_k_ff_2_q), .Qn(j_k_ff_2_qn), .reset(button_1_out));  // open: preset
  and and_6 (and_6_out, j_k_ff_5_qn, j_k_ff_4_qn, j_k_ff_2_qn, j_k_ff_1_qn);
  and and_7 (and_7_out, j_k_ff_5_qn, j_k_ff_4_qn, j_k_ff_3_qn, j_k_ff_2_qn, j_k_ff_1_q);
  J_K_Flip_Flop j_k_ff_3 (
    .J(and_7_out), .K(and_6_out), .clk(and_1_out), .Q(j_k_ff_3_q), .Qn(j_k_ff_3_qn), .reset(button_1_out));  // open: preset
  and and_8 (and_8_out, j_k_ff_5_qn, j_k_ff_3_qn, j_k_ff_2_qn, j_k_ff_1_qn);
  and and_9 (and_9_out, j_k_ff_5_qn, j_k_ff_4_qn, j_k_ff_2_qn, j_k_ff_1_qn, j_k_ff_3_q);
  J_K_Flip_Flop j_k_ff_4 (
    .J(and_9_out), .K(and_8_out), .clk(and_1_out), .Q(j_k_ff_4_q), .Qn(j_k_ff_4_qn), .reset(button_1_out));  // open: preset
  and and_10 (and_10_out, j_k_ff_4_qn, j_k_ff_2_qn, j_k_ff_1_qn, j_k_ff_3_q);
  and and_11 (and_11_out, j_k_ff_5_qn, j_k_ff_4_qn, j_k_ff_3_qn, j_k_ff_2_qn, j_k_ff_1_q);
  J_K_Flip_Flop j_k_ff_5 (
    .J(and_11_out), .K(and_10_out), .clk(and_1_out), .Q(j_k_ff_5_q), .Qn(j_k_ff_5_qn), .reset(button_1_out));  // open: preset

  // Notes on the sheet:
  //   c
  //   b
  //   a
  //   x
  //   Z
endmodule

module Old_control_unit_Xno_use (
  input  B,
  input  A,
  input  E,
  input  in_4,
  input  in_5,
  input  M_reset,
  output SR8_clock,
  output TR_clock,
  output TR_res,
  output SR8_DE,
  output SR8_w_f4,
  output SR8_QE
);

  wire and_1_out, and_2_out, and_3_out, and_4_out, and_5_out, and_6_out, and_7_out, and_8_out, and_9_out,
       and_10_out, and_11_out, and_12_out, and_13_out, and_14_out, and_15_out, and_16_out, and_17_out,
       and_18_out, and_19_out, and_20_out, and_21_out, and_22_out, and_23_out, and_24_out, clock_1_out,
       clock_2_out, d_ff_1_q, d_ff_2_q, d_ff_3_q, d_ff_4_q, d_ff_5_q, d_ff_6_q, d_ff_7_q, d_ff_8_q, d_ff_9_q,
       demux_4_bits_1_q00, demux_4_bits_1_q01, demux_4_bits_1_q10, j_k_ff_1_q, j_k_ff_1_qn, j_k_ff_2_q,
       j_k_ff_2_qn, j_k_ff_3_q, j_k_ff_3_qn, j_k_ff_4_q, j_k_ff_4_qn, j_k_ff_5_q, j_k_ff_5_qn, j_k_ff_6_qn,
       j_k_ff_7_qn, j_k_ff_8_qn, j_k_ff_9_q, j_k_ff_9_qn, j_k_ff_10_qn, j_k_ff_11_qn, not_1_out, not_2_out,
       not_3_out, or_1_out, or_2_out, or_3_out, or_4_out, or_5_out, or_6_out, or_7_out, or_8_out, or_9_out,
       undriven;

  D_Flip_Flop d_ff_1 (.D(or_1_out), .clk(or_2_out), .Q(d_ff_1_q), .reset(undriven));  // open: Qn, preset
  or or_1 (or_1_out, d_ff_2_q, in_4);
  or or_2 (or_2_out, in_5, d_ff_9_q);
  D_Flip_Flop d_ff_2 (.D(d_ff_1_q), .clk(or_2_out), .Q(d_ff_2_q), .reset(undriven));  // open: Qn, preset
  demux_4_bits demux_4_bits_1 (
    .A(A), .B(B), .E(E), .Q00(demux_4_bits_1_q00), .Q01(demux_4_bits_1_q01), .Q10(demux_4_bits_1_q10));  // open: Q11
  Clock clock_1 (.out(clock_1_out));
  not not_1 (not_1_out, j_k_ff_5_q);
  or or_3 (or_3_out, j_k_ff_2_q, SR8_clock);
  and and_1 (and_1_out, clock_1_out, not_1_out);
  D_Flip_Flop d_ff_3 (.D(j_k_ff_4_q), .clk(or_3_out), .Q(d_ff_3_q), .reset(or_5_out));  // open: Qn, preset
  and and_2 (and_2_out, demux_4_bits_1_q10, and_1_out);
  not not_2 (not_2_out, d_ff_9_q);
  or or_4 (or_4_out, d_ff_9_q, M_reset);
  Clock clock_2 (.out(clock_2_out));
  D_Flip_Flop d_ff_4 (.D(d_ff_3_q), .clk(or_3_out), .Q(d_ff_4_q), .reset(or_5_out));  // open: Qn, preset
  and and_3 (and_3_out, and_2_out, not_2_out);
  and and_4 (and_4_out, d_ff_8_q, clock_2_out);
  not not_3 (not_3_out, d_ff_7_q);
  LED led_1 (.in(TR_res));
  LED led_2 (.in(TR_clock));
  LED led_3 (.in(j_k_ff_9_q));
  D_Flip_Flop d_ff_5 (.D(d_ff_4_q), .clk(or_3_out), .Q(d_ff_5_q), .reset(or_5_out));  // open: Qn, preset
  and and_5 (and_5_out, j_k_ff_5_qn, j_k_ff_4_qn, j_k_ff_2_qn);
  J_K_Flip_Flop j_k_ff_1 (
    .J(and_5_out), .K(and_5_out), .clk(and_3_out), .Q(j_k_ff_1_q), .Qn(j_k_ff_1_qn), .reset(or_4_out));  // open: preset
  and and_6 (and_6_out, and_4_out, not_3_out);
  LED led_4 (.in(SR8_w_f4));
  LED led_5 (.in(SR8_DE));
  LED led_6 (.in(SR8_clock));
  LED led_7 (.in(j_k_ff_3_q));
  D_Flip_Flop d_ff_6 (.D(d_ff_5_q), .clk(or_3_out), .Q(d_ff_6_q), .reset(or_5_out));  // open: Qn, preset
  or or_5 (or_5_out, j_k_ff_1_q, M_reset);
  D_Flip_Flop d_ff_7 (.D(d_ff_6_q), .clk(or_3_out), .Q(d_ff_7_q), .reset(or_5_out));  // open: Qn, preset
  and and_7 (and_7_out, j_k_ff_5_qn, j_k_ff_1_qn, j_k_ff_4_q);
  J_K_Flip_Flop j_k_ff_2 (
    .J(and_7_out), .K(and_7_out), .clk(and_3_out), .Q(j_k_ff_2_q), .Qn(j_k_ff_2_qn), .reset(or_4_out));  // open: preset
  and and_8 (and_8_out, j_k_ff_3_qn, j_k_ff_6_qn, j_k_ff_7_qn, j_k_ff_8_qn, j_k_ff_11_qn, TR_clock, j_k_ff_9_q);
  and and_9 (and_9_out, j_k_ff_3_qn, j_k_ff_6_qn, j_k_ff_9_qn, SR8_w_f4, j_k_ff_10_qn, j_k_ff_11_qn, SR8_DE);
  or or_6 (or_6_out, j_k_ff_2_q, d_ff_7_q);
  or or_7 (or_7_out, and_9_out, and_8_out);
  and and_10 (and_10_out, j_k_ff_11_qn, j_k_ff_10_qn, j_k_ff_8_qn, j_k_ff_7_qn, j_k_ff_6_qn);
  or or_8 (or_8_out, j_k_ff_4_q, d_ff_9_q);
  and and_11 (and_11_out, j_k_ff_2_qn, j_k_ff_1_qn, j_k_ff_4_q, j_k_ff_5_q);
  J_K_Flip_Flop j_k_ff_3 (
    .J(or_7_out), .K(and_10_out), .clk(and_6_out), .Q(j_k_ff_3_q), .Qn(j_k_ff_3_qn), .reset(or_5_out));  // open: preset
  D_Flip_Flop d_ff_8 (.D(or_8_out), .clk(or_6_out), .Q(d_ff_8_q), .reset(or_5_out));  // open: Qn, preset
  and and_12 (and_12_out, j_k_ff_5_qn, j_k_ff_4_qn, j_k_ff_2_qn, j_k_ff_1_q);
  J_K_Flip_Flop j_k_ff_4 (
    .J(and_12_out), .K(and_11_out), .clk(and_3_out), .Q(j_k_ff_4_q), .Qn(j_k_ff_4_qn), .reset(or_4_out));  // open: preset
  D_Flip_Flop d_ff_9 (.D(d_ff_8_q), .clk(or_6_out), .Q(d_ff_9_q), .reset(or_5_out));  // open: Qn, preset
  and and_13 (and_13_out, j_k_ff_2_qn, j_k_ff_1_qn, j_k_ff_4_q);
  and and_14 (and_14_out, j_k_ff_6_qn, j_k_ff_7_qn, j_k_ff_8_qn, j_k_ff_9_qn, j_k_ff_10_qn, j_k_ff_11_qn, j_k_ff_3_q);
  and and_15 (and_15_out, j_k_ff_5_qn, j_k_ff_1_qn, j_k_ff_2_q, j_k_ff_4_q);
  J_K_Flip_Flop j_k_ff_5 (
    .J(and_15_out), .K(and_13_out), .clk(and_3_out), .Q(j_k_ff_5_q), .Qn(j_k_ff_5_qn), .reset(or_4_out));  // open: preset
  and and_16 (and_16_out, j_k_ff_3_qn, j_k_ff_7_qn, j_k_ff_8_qn, j_k_ff_9_qn, j_k_ff_10_qn, j_k_ff_11_qn);
  J_K_Flip_Flop j_k_ff_6 (
    .J(and_14_out), .K(and_16_out), .clk(and_6_out), .Q(SR8_clock), .Qn(j_k_ff_6_qn), .reset(or_9_out));  // open: preset
  or or_9 (or_9_out, d_ff_9_q, or_5_out);
  and and_17 (and_17_out, j_k_ff_6_qn, j_k_ff_7_qn, j_k_ff_8_qn, j_k_ff_10_qn, j_k_ff_11_qn, j_k_ff_9_q, j_k_ff_3_q);
  J_K_Flip_Flop j_k_ff_7 (
    .J(and_17_out), .K(and_18_out), .clk(and_6_out), .Q(SR8_DE), .Qn(j_k_ff_7_qn), .reset(or_5_out));  // open: preset
  and and_18 (and_18_out, j_k_ff_6_qn, j_k_ff_8_qn, j_k_ff_9_qn, j_k_ff_10_qn, j_k_ff_11_qn, j_k_ff_3_q);
  and and_19 (and_19_out, j_k_ff_3_qn, j_k_ff_6_qn, j_k_ff_9_qn, j_k_ff_10_qn, j_k_ff_11_qn, SR8_DE);
  J_K_Flip_Flop j_k_ff_8 (
    .J(and_19_out), .K(and_19_out), .clk(and_6_out), .Q(SR8_w_f4), .Qn(j_k_ff_8_qn), .reset(or_5_out));  // open: preset
  and and_20 (and_20_out, j_k_ff_3_qn, j_k_ff_6_qn, j_k_ff_7_qn, j_k_ff_8_qn, j_k_ff_9_qn, j_k_ff_10_qn, TR_res);
  and and_21 (and_21_out, j_k_ff_6_qn, j_k_ff_7_qn, j_k_ff_8_qn, j_k_ff_10_qn, j_k_ff_11_qn, j_k_ff_3_q);
  J_K_Flip_Flop j_k_ff_9 (
    .J(and_20_out), .K(and_21_out), .clk(and_6_out), .Q(j_k_ff_9_q), .Qn(j_k_ff_9_qn), .reset(or_5_out));  // open: preset
  or or_10 (SR8_QE, d_ff_9_q, j_k_ff_9_q);
  and and_22 (and_22_out, j_k_ff_3_qn, j_k_ff_6_qn, j_k_ff_7_qn, j_k_ff_8_qn, j_k_ff_11_qn, j_k_ff_9_q);
  and and_23 (and_23_out, j_k_ff_3_qn, j_k_ff_6_qn, j_k_ff_7_qn, j_k_ff_8_qn, j_k_ff_11_qn, j_k_ff_9_q);
  J_K_Flip_Flop j_k_ff_10 (
    .J(and_22_out), .K(and_23_out), .clk(and_6_out), .Q(TR_clock), .Qn(j_k_ff_10_qn), .reset(or_5_out));  // open: preset
  and and_24 (and_24_out, j_k_ff_3_qn, j_k_ff_6_qn, j_k_ff_7_qn, j_k_ff_8_qn, j_k_ff_9_qn, j_k_ff_10_qn);
  J_K_Flip_Flop j_k_ff_11 (
    .J(and_24_out), .K(and_24_out), .clk(and_6_out), .Q(TR_res), .Qn(j_k_ff_11_qn), .reset(or_5_out));  // open: preset

  // Notes on the sheet:
  //   c
  //   Reset
  //   b
  //   a
  //   X
  //   x
  //   A
  //   Registro de control de multiplicacion
  //   B
  //   C
  //   D
  //   E
  //   Anthony Lopez 3-743-1884
  //   F
endmodule

module guardar_data (
  input  boton,
  output SR4_Reset,
  output Clock_store,
  output SR4_DE,
  output Z
);

  wire and_1_out, and_2_out, and_3_out, and_4_out, and_5_out, and_6_out, and_7_out, and_8_out, and_9_out,
       and_10_out, clock_1_out, j_k_ff_1_qn, j_k_ff_2_qn, j_k_ff_3_qn, j_k_ff_4_q, j_k_ff_4_qn, j_k_ff_5_qn,
       not_1_out;

  not not_1 (not_1_out, j_k_ff_4_q);
  Clock clock_1 (.out(clock_1_out));
  and and_1 (and_1_out, not_1_out, clock_1_out);
  LED led_1 (.in(SR4_Reset));
  LED led_2 (.in(Clock_store));
  LED led_3 (.in(SR4_DE));
  LED led_4 (.in(j_k_ff_4_q));
  LED led_5 (.in(Z));
  and and_2 (and_2_out, j_k_ff_5_qn, j_k_ff_4_qn, j_k_ff_3_qn, j_k_ff_2_qn);
  J_K_Flip_Flop j_k_ff_1 (
    .J(and_2_out), .K(and_2_out), .clk(and_1_out), .Q(SR4_Reset), .Qn(j_k_ff_1_qn), .reset(boton));  // open: preset
  and and_3 (and_3_out, j_k_ff_5_qn, j_k_ff_4_qn, j_k_ff_1_qn, SR4_DE);
  and and_4 (and_4_out, j_k_ff_4_qn, j_k_ff_2_qn, j_k_ff_1_qn, SR4_DE, Z);
  J_K_Flip_Flop j_k_ff_2 (
    .J(and_4_out), .K(and_3_out), .clk(and_1_out), .Q(Clock_store), .Qn(j_k_ff_2_qn), .reset(boton));  // open: preset
  and and_5 (and_5_out, j_k_ff_5_qn, j_k_ff_4_qn, j_k_ff_2_qn, j_k_ff_1_qn);
  and and_6 (and_6_out, j_k_ff_5_qn, j_k_ff_4_qn, j_k_ff_3_qn, j_k_ff_2_qn, SR4_Reset);
  J_K_Flip_Flop j_k_ff_3 (
    .J(and_6_out), .K(and_5_out), .clk(and_1_out), .Q(SR4_DE), .Qn(j_k_ff_3_qn), .reset(boton));  // open: preset
  and and_7 (and_7_out, j_k_ff_5_qn, j_k_ff_3_qn, j_k_ff_2_qn, j_k_ff_1_qn);
  and and_8 (and_8_out, j_k_ff_5_qn, j_k_ff_4_qn, j_k_ff_2_qn, j_k_ff_1_qn, SR4_DE);
  J_K_Flip_Flop j_k_ff_4 (
    .J(and_8_out), .K(and_7_out), .clk(and_1_out), .Q(j_k_ff_4_q), .Qn(j_k_ff_4_qn), .reset(boton));  // open: preset
  and and_9 (and_9_out, j_k_ff_4_qn, j_k_ff_2_qn, j_k_ff_1_qn, SR4_DE);
  and and_10 (and_10_out, j_k_ff_5_qn, j_k_ff_4_qn, j_k_ff_3_qn, j_k_ff_2_qn, SR4_Reset);
  J_K_Flip_Flop j_k_ff_5 (
    .J(and_10_out), .K(and_9_out), .clk(and_1_out), .Q(Z), .Qn(j_k_ff_5_qn), .reset(boton));  // open: preset

  // Notes on the sheet:
  //   c
  //   b
  //   a
  //   x
  //   Z
endmodule

module binay_to_BCD (
  input  D0,
  input  D1,
  input  D2,
  input  D3,
  output Q0,
  output Q1,
  output Q2,
  output Q3
);

  wire not_1_out, not_2_out, or_1_out, or_2_out, or_3_out, or_4_out, or_5_out, xor_1_out, xor_2_out;

  xor xor_1 (xor_1_out, D1, D3);
  or or_1 (or_1_out, D2, D3);
  not not_1 (not_1_out, or_1_out);
  xor xor_2 (xor_2_out, D3, D0);
  or or_2 (or_2_out, xor_1_out, xor_2_out);
  not not_2 (not_2_out, or_2_out);
  or or_3 (or_3_out, xor_2_out, not_1_out);
  or or_4 (or_4_out, not_1_out, not_2_out);
  not not_3 (Q3, or_4_out);
  xor xor_3 (Q0, D0, Q3);
  and and_1 (Q1, xor_1_out, or_3_out);
  or or_5 (or_5_out, D1, or_3_out);
  not not_4 (Q2, or_5_out);
endmodule

module double_dable (
  input  D0,
  input  D1,
  input  D2,
  input  D3,
  input  D4,
  input  D5,
  input  D6,
  input  D7,
  output Un0,
  output Un1,
  output Un2,
  output Un3,
  output Dec0,
  output Dec1,
  output Dec2,
  output Dec3,
  output Cen0,
  output Cen1,
  output Cen2,
  output Cen3
);

  wire binay_to_bcd_1_q0, binay_to_bcd_1_q1, binay_to_bcd_1_q2, binay_to_bcd_1_q3, binay_to_bcd_2_q0,
       binay_to_bcd_2_q1, binay_to_bcd_2_q2, binay_to_bcd_2_q3, binay_to_bcd_3_q0, binay_to_bcd_3_q1,
       binay_to_bcd_3_q2, binay_to_bcd_3_q3, binay_to_bcd_4_q0, binay_to_bcd_4_q1, binay_to_bcd_4_q2,
       binay_to_bcd_4_q3, binay_to_bcd_5_q0, binay_to_bcd_5_q1, binay_to_bcd_5_q2;

  binay_to_BCD binay_to_bcd_1 (
    .D0(D5), .D1(D6), .D2(D7), .Q0(binay_to_bcd_1_q0), .Q1(binay_to_bcd_1_q1), .Q2(binay_to_bcd_1_q2),
    .Q3(binay_to_bcd_1_q3));  // open: D3
  binay_to_BCD binay_to_bcd_2 (
    .D0(D4), .D1(binay_to_bcd_1_q0), .D2(binay_to_bcd_1_q1), .D3(binay_to_bcd_1_q2), .Q0(binay_to_bcd_2_q0),
    .Q1(binay_to_bcd_2_q1), .Q2(binay_to_bcd_2_q2), .Q3(binay_to_bcd_2_q3));
  binay_to_BCD binay_to_bcd_3 (
    .D0(D3), .D1(binay_to_bcd_2_q0), .D2(binay_to_bcd_2_q1), .D3(binay_to_bcd_2_q2), .Q0(binay_to_bcd_3_q0),
    .Q1(binay_to_bcd_3_q1), .Q2(binay_to_bcd_3_q2), .Q3(binay_to_bcd_3_q3));
  binay_to_BCD binay_to_bcd_4 (
    .D0(D2), .D1(binay_to_bcd_3_q0), .D2(binay_to_bcd_3_q1), .D3(binay_to_bcd_3_q2), .Q0(binay_to_bcd_4_q0),
    .Q1(binay_to_bcd_4_q1), .Q2(binay_to_bcd_4_q2), .Q3(binay_to_bcd_4_q3));
  binay_to_BCD binay_to_bcd_5 (
    .D0(binay_to_bcd_3_q3), .D1(binay_to_bcd_2_q3), .D2(binay_to_bcd_1_q3), .Q0(binay_to_bcd_5_q0),
    .Q1(binay_to_bcd_5_q1), .Q2(binay_to_bcd_5_q2), .Q3(Cen1));  // open: D3
  binay_to_BCD binay_to_bcd_6 (
    .D0(D1), .D1(binay_to_bcd_4_q0), .D2(binay_to_bcd_4_q1), .D3(binay_to_bcd_4_q2), .Q0(Un1), .Q1(Un2),
    .Q2(Un3), .Q3(Dec0));
  binay_to_BCD binay_to_bcd_7 (
    .D0(binay_to_bcd_4_q3), .D1(binay_to_bcd_5_q0), .D2(binay_to_bcd_5_q1), .D3(binay_to_bcd_5_q2),
    .Q0(Dec1), .Q1(Dec2), .Q2(Dec3), .Q3(Cen0));

  assign Un0 = D0;
endmodule
